// Logisim project InputLogicMicroprogram.circ as structural Verilog: 1 circuit, main circuit main
module main (
  input  I1,
  input  I0,
  input  T,
  output S1,
  output S0,
  output LD
);

  wire not_1_out;

  not not_1 (not_1_out, I1);
  Multiplexer #(.select(3)) multiplexer_1 (
    .in0(1'b0), .in1(1'b0), .in2(1'b0), .in3(1'b0), .in4(1'b1), .in5(1'b1), .in6(1'b1), .in7(1'b1), .out(S1),
    .sel({I1, I0, T}));  // open: en
  Multiplexer #(.select(3)) multiplexer_2 (
    .in0(1'b0), .in1(1'b1), .in2(1'b0), .in3(1'b1), .in4(1'b0), .in5(1'b0), .in6(1'b1), .in7(1'b1), .out(S0),
    .sel({I1, I0, T}));  // open: en
  and and_1 (LD, not_1_out, I0, T);
endmodule
