// Logisim project MAIN CIRCUIT.circ as structural Verilog: 1 circuit, main circuit main
module main (
  output [10:0] AR,
  output [10:0] PC,
  output [6:0] SBR,
  output [6:0] CAR,
  output [15:0] DR,
  output [15:0] AC,
  output O,
  output U
);

  wire AR_p4, AR_p5, Control_p1, Control_p3, Control_p5, main_1_p13, main_1_p14, main_1_p15, or_1_out,
       or_2_out;
  wire [1:0] main_1_p8, main_1_p20, priority_encoder_1_p3, undriven;
  wire [10:0] main_1_p4, multiplexer_1_out;
  wire [15:0] multiplexer_2_out, RAM_p6;

  Multiplexer #(.width(11)) multiplexer_1 (
    .in0(PC), .in1(DR[10:0]), .out(multiplexer_1_out), .sel(undriven[0]), .en(AR_p4));
  or or_1 (or_1_out, undriven[1], undriven[0]);
  // _11BitRegister_main AR: pin names not known; wires that end beside it: 1'b0, or_1_out, 1'b0, AR_p4, AR_p5, multiplexer_1_out, AR, AR
  // _11BitRegister_main PC: pin names not known; wires that end beside it: AR_p5, PC
  // main_main Control: pin names not known; wires that end beside it: Control_p1, AC, Control_p3, DR, Control_p5, AR_p5, SBR, CAR
  // DecodeMicropLogic_main main_1: pin names not known; wires that end beside it: Control_p1, Control_p3, Control_p5, main_1_p4[0], main_1_p4[1], main_1_p4[2], main_1_p4[3], main_1_p8[0], main_1_p4[4], main_1_p4[5], main_1_p4[6], main_1_p8[1], main_1_p13, main_1_p14, main_1_p15, main_1_p4[7], main_1_p4[8], main_1_p4[9], main_1_p4[10], main_1_p20[0], main_1_p20[1]
  // Priority_Encoder #(.select(2)) priority_encoder_1: pin names not known; wires that end beside it: main_1_p15, main_1_p8[1], priority_encoder_1_p3, main_1_p13, 1'b0
  or or_2 (or_2_out, main_1_p15, main_1_p8[1], main_1_p13);
  // Ram2048X16_main RAM: pin names not known; wires that end beside it: main_1_p8[0], main_1_p8[1], DR, AR_p5, AR, RAM_p6
  Multiplexer #(.select(2), .width(16)) multiplexer_2 (
    .in0({{5{1'b0}}, PC}), .in1(RAM_p6), .in2(AC), .out(multiplexer_2_out), .sel(priority_encoder_1_p3));  // open: in3, en
  // _16BitRegister_main DR: pin names not known; wires that end beside it: main_1_p14, or_2_out, AR_p5, multiplexer_2_out, DR
  Clock clk (.out(AR_p5));
  // ALU_main main_2: pin names not known; wires that end beside it: main_1_p4, AR_p5, DR, AC, O, U
endmodule
